# Fritzing sketch adafruit_proto_cape (saved by Fritzing 0.9.3b)
circuit board: 8.46667cm x 5.64444cm

parts:
  Part1 = Adafruit BeagleBone Proto Cape [part_number="Adafruit #572"]
  IC1 = MCP3008 8-channel 10-bit ADC [part_number=MCP3008]

nets:
  N1: Part1.SPI1_D0, Part1.1#248
  N2: Part1.GPIO_115, Part1.1#237
  N3: Part1.GND, Part1.1#92, Part1.1#226
  N4: Part1.GPIO1_CS0, Part1.1#259
  N5: Part1.GPIO_112, Part1.1#160, Part1.1#270
  N6: Part1.2#93, Part1.5#274, IC1.no_name_yet#4, IC1.no_name_yet#14
  N7: Part1.5#96, IC1.no_name_yet#3
  N8: Part1.1#103, Part1.3.3V, Part1.1#289
  N9: Part1.2#104, IC1.no_name_yet#15
  N10: Part1.5#107, IC1.no_name_yet#2
  N11: Part1.2#227, IC1.no_name_yet#9
  N12: Part1.5#230, IC1.no_name_yet#8
  N13: Part1.2#238, IC1.no_name_yet#10
  N14: Part1.5#241, IC1.no_name_yet#7
  N15: Part1.2#249, IC1.no_name_yet#11
  N16: Part1.5#252, IC1.no_name_yet#6
  N17: Part1.2#260, IC1.no_name_yet#12
  N18: Part1.5#263, IC1.no_name_yet#5
  N19: Part1.2#271, IC1.no_name_yet#13
  N20: Part1.2#290, IC1.no_name_yet#16
  N21: Part1.5#293, IC1.no_name_yet#1

notes:
  BREADBOARD ADC CAPE

custom parts:
  Adafruit BeagleBone Proto Cape: Add some circuitry to your Beagle Bone or Beagle Bone Black with our lovely Proto Cape. If you have a 'Bone you need one of these! This PCB fits neatly on top of a Beagle Bone, without getting in the way of the Ethernet jack, and provides a breakout to both 46 pin headers - with individual numbering to keep them straight. We also threw down some strips to access the 5V and 3V power supplies as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
