# Fritzing sketch pru_adc_schematic (saved by Fritzing 0.9.3b)
breadboards: 1

parts:
  IC1 = MCP3008 8-channel 10-bit ADC [part_number=MCP3008]

nets:
  Analog Input: IC1.no_name_yet#1
  GND: IC1.no_name_yet#9, IC1.no_name_yet#14
  CHIPSELECT: IC1.no_name_yet#10
  MISO: IC1.no_name_yet#11
  MOSI: IC1.no_name_yet#12
  CLK: IC1.no_name_yet#13
  3.3V: IC1.no_name_yet#15, IC1.no_name_yet#16

notes:
  PRU-ADC
  P9_30
  P9_27
  P9_28
  P9_29
  TO BBB P9 HEADER
